# Fritzing sketch IOT_MainBoard_00 (saved by Fritzing 0.9.4)
circuit board: 2.3cm x 2.5cm
circuit board: 1.25cm x 7cm
circuit board: 2.5cm x 10cm
breadboards: 1

parts:
  IC1 = LQFP-32 [chip_label=IC package=LQFP]
  C1 = Electrolytic Capacitor [capacitance=1µF package="200 mil [THT, electrolytic]"]
  J1 = female pin header, 5 pins [form="♀ (female)"]  # not connected
  J4 = female pin header, 6 pins [form="♀ (female)"]  # not connected
  IC2 = SO08 [chip_label=IC package=SO]  # not connected
  XTAL1 = CRYSTAL - kHz [frequency="32 kHz"]  # not connected
  C2 = Ceramic Capacitor [capacitance=100nF package="0805 [SMD, multilayer]"]  # not connected
  R1 = Resistor [tolerance=±5% resistance=220 package="0805 [SMD]"]  # not connected
  S1 = Pushbutton [package="[THT]"]  # not connected
  U1 = V_REG_MIC5235 [package=sot23-5]  # not connected
  C3 = Tantalum Capacitor [capacitance=1μF package="B 3528 [SMD, tantalum]"]  # not connected
  RFM1 = RFM69HCW ISM Transciever  # not connected
  C4 = Tantalum Capacitor [capacitance=1μF package="B 3528 [SMD, tantalum]"]  # not connected
  Pad2 = Pad [width=2.5 height=2.5 connect=center]
  Pad3 = Pad [width=2.5 height=2.5 connect=center]
  J8 = female pin header, 6 pins [form="♀ (female)"]  # not connected
  R2 = Resistor [tolerance=±5% resistance=220 package="0805 [SMD]"]  # not connected
  C5 = Ceramic Capacitor [capacitance=100nF package="0805 [SMD, multilayer]"]  # not connected
  J11 = female pin header, 1 pin [form="♀ (female)"]  # not connected
  J12 = female pin header, 1 pin [form="♀ (female)"]
  J6 = female pin header, 13 pins [form="♀ (female)"]
  J10 = female pin header, 13 pins [form="♀ (female)"]
  R3 = Resistor [tolerance=±5% resistance=220 package="0805 [SMD]"]  # not connected

nets:
  N1: IC1.1, J10.pin6
  N2: IC1.2, J10.pin5
  N3: IC1.4, IC1.6
  N4: IC1.7, Pad2.pad
  N5: IC1.8, Pad3.pad
  N6: IC1.9, J6.pin4
  N7: IC1.10, J6.pin5
  N8: IC1.11, J6.pin6
  N9: IC1.12, J6.pin7
  N10: IC1.13, J6.pin8
  N11: IC1.14, J6.pin9
  N12: IC1.15, J6.pin10
  N13: IC1.16, J6.pin11
  N14: IC1.17, J6.pin12
  N15: IC1.25, J10.pin13
  N16: IC1.26, J10.pin12
  N17: IC1.27, J10.pin11
  N18: IC1.28, J10.pin10
  N19: IC1.30, J10.pin9
  N20: IC1.31, J10.pin8
  N21: IC1.32, J10.pin7
  N22: C1.+, J12.pin1

notes:
  Passives:
  10K - Reset High
  10K - SDA PullUp
  10K - SCL PullUp
  Pins:
  7-RX
  8-TX
  4-DTR
  A3-RST
  3-RING
  2-SQW
  A4-SDA
  A5-SCL
  0-RX
  1-TX
  0,1,2,3,5,6,9,10,11,12,13, A0, A1, A2,A4,A5
  A2
  4K - LED Res
  RED - LED
  13 - LED

custom parts:
  RFM69HCW ISM Transciever: RF Transceiver by Hope RF. Well supported Arduino libraries are available. This ISM band transceiver is available in several frequencies e.g. 433MHz and 915MHz and it is also available in various feature versions.
