# Fritzing sketch IOT_MainBoard_02 (saved by Fritzing 0.9.4)
circuit board: 2cm x 7.5cm
circuit board: 2.5cm x 2.3cm
circuit board: 3cm x 15.4cm
circuit board: 2cm x 7.5cm
breadboards: 1

parts:
  C1 = Electrolytic Capacitor [capacitance=1µF package="200 mil [THT, electrolytic]"]  # not connected
  J4 = female pin header, 6 pins [form="♀ (female)"]  # not connected
  IC2 = SO08 [chip_label=IC package=SO]
  XTAL1 = CRYSTAL - kHz [frequency="32 kHz"]
  C2 = Ceramic Capacitor [capacitance=100nF package="0805 [SMD, multilayer]"]  # not connected
  R1 = Resistor [tolerance=±5% resistance=220 package="0805 [SMD]"]
  S1 = Pushbutton [package="[THT]"]  # not connected
  RFM1 = RFM69HCW ISM Transciever  # not connected
  J8 = female pin header, 6 pins [form="♀ (female)"]  # not connected
  R2 = Resistor [tolerance=±5% resistance=220 package="0805 [SMD]"]
  C5 = Ceramic Capacitor [capacitance=100nF package="0805 [SMD, multilayer]"]  # not connected
  J11 = female pin header, 1 pin [form="♀ (female)"]  # not connected
  J12 = female pin header, 1 pin [form="♀ (female)"]
  Part1 = Arduino Pro Mini v13
  J13 = female pin header, 13 pins [form="♀ (female)"]
  J14 = female pin header, 13 pins [form="♀ (female)"]
  J15 = female pin header, 2 pins [form="♀ (female)"]  # not connected
  R3 = Resistor [tolerance=±5% resistance=220 package="0805 [SMD]"]
  IC3 = SO08 [chip_label=IC package=SO]  # not connected
  J16 = female pin header, 1 pin [form="♀ (female)"]  # not connected
  J17 = female pin header, 1 pin [form="♀ (female)"]  # not connected
  J18 = female pin header, 1 pin [form="♀ (female)"]  # not connected
  LED1 = smd LED [color="Red (633nm)" package="0805 [SMD]"]  # not connected
  LED2 = smd LED [color="Red (633nm)" package="0805 [SMD]"]  # not connected
  LED3 = smd LED [color="Red (633nm)" package="0805 [SMD]"]  # not connected
  LED4 = smd LED [color="Red (633nm)" package="0805 [SMD]"]  # not connected
  LED5 = smd LED [color="Red (633nm)" package="0805 [SMD]"]  # not connected
  LED6 = smd LED [color="Red (633nm)" package="0805 [SMD]"]  # not connected

nets:
  N1: IC2.1, XTAL1.pin_1
  N2: IC2.2, XTAL1.pin_0
  N3: IC2.5, R1.Pin_0, Part1.A4
  N4: IC2.6, R2.Pin_1, Part1.A5
  N5: IC2.8, R3.Pin_0
  N6: R2.Pin_0, Part1.VCC, J14.pin9
  N7: J12.pin1, R3.Pin_1
  N8: Part1.GND, J13.pin9, J13.pin13, J14.pin11
  N9: Part1.RAW, J14.pin12, J14.pin13
  N10: Part1.RESET, J13.pin10, J14.pin10
  N11: Part1.A3, J14.pin8
  N12: Part1.A2, J14.pin7
  N13: Part1.A1, J14.pin6
  N14: Part1.A0, J14.pin5
  N15: Part1.D13/SCK, J14.pin4
  N16: Part1.D12/MISO, J14.pin3
  N17: Part1.D11_PWM/MOSI, J14.pin2
  N18: Part1.D10_PWM/SS, J14.pin1
  N19: Part1.D9_PWM, J13.pin1
  N20: Part1.D8, J13.pin2
  N21: Part1.D7, J13.pin3
  N22: Part1.D6_PWM, J13.pin4
  N23: Part1.D5_PWM, J13.pin5
  N24: Part1.D4, J13.pin6
  N25: Part1.D3_PWM, J13.pin7
  N26: Part1.D2, J13.pin8
  N27: Part1.D1/RX, J13.pin11
  N28: Part1.D0/TX, J13.pin12

notes:
  Passives:
  10K - SDA PullUp
  10K - SCL PullUp
  1K - RTC Pow

custom parts:
  RFM69HCW ISM Transciever: RF Transceiver by Hope RF. Well supported Arduino libraries are available. This ISM band transceiver is available in several frequencies e.g. 433MHz and 915MHz and it is also available in various feature versions.
